// Logisim project circuitos_utiles.circ as structural Verilog: 8 circuits, main circuit main
module main (
  input  in_1
);
endmodule

module flipflop_sr_async (
  input  S,
  input  R,
  output Q,
  output notQ
);

  nor nor_1 (notQ, S, Q);
  nor nor_2 (Q, notQ, R);
endmodule

module flipflop_sr_sync (
  input  clk,
  input  S,
  input  R,
  output Q,
  output notQ
);

  wire and_1_out, and_2_out;

  and and_1 (and_1_out, clk, S);
  and and_2 (and_2_out, R, clk);
  flipflop_sr_async flipflop_sr_async_1 (.S(and_1_out), .R(and_2_out), .Q(Q), .notQ(notQ));
endmodule

module flipflop_d_sync (
  input  D,
  input  clk,
  output Q,
  output notQ
);

  wire and_1_out, and_2_out, not_1_out;

  not not_1 (not_1_out, D);
  and and_1 (and_1_out, D, clk);
  and and_2 (and_2_out, clk, not_1_out);
  nor nor_1 (notQ, and_1_out, Q);
  nor nor_2 (Q, notQ, and_2_out);
endmodule

module flipflop_jk_sync (
  input  J,
  input  clk,
  input  K,
  input  J_2,
  input  clk_2,
  input  K_2,
  output Q,
  output notQ,
  output Q_2,
  output notQ_2
);

  wire and_1_out, and_2_out, and_3_out, and_4_out, nand_1_out, nand_2_out;

  and and_1 (and_1_out, notQ_2, J_2);
  nand nand_1 (nand_1_out, and_1_out, clk_2);
  nand nand_2 (nand_2_out, clk_2, and_2_out);
  and and_2 (and_2_out, K_2, Q_2);
  nand nand_3 (Q_2, nand_1_out, notQ_2);
  nand nand_4 (notQ_2, Q_2, nand_2_out);
  and and_3 (and_3_out, notQ, J);
  and and_4 (and_4_out, K, Q);
  flipflop_sr_sync flipflop_sr_sync_1 (.S(and_3_out), .R(and_4_out), .clk(clk), .Q(Q), .notQ(notQ));
endmodule

module registro_simple (
  input  i,
  input  clk,
  input  load,
  output S0
);

  wire and_1_out, and_2_out, not_1_out, or_1_out;

  and and_1 (and_1_out, i, load);
  not not_1 (not_1_out, load);
  and and_2 (and_2_out, not_1_out, S0);
  or or_1 (or_1_out, and_1_out, and_2_out);
  flipflop_d_sync flipflop_d_sync_1 (.D(or_1_out), .clk(clk), .Q(S0));  // open: notQ
endmodule

module registro_salida_restringida (
  input  clk,
  input  i,
  input  load,
  input  read,
  output s0
);

  wire and_1_out, registro_simple_1_s0;

  and and_1 (and_1_out, clk, read);
  registro_simple registro_simple_1 (.i(i), .load(load), .clk(clk), .S0(registro_simple_1_s0));
  assign s0 = and_1_out ? registro_simple_1_s0 : 1'bz;  // Controlled_Buffer controlled_buffer_1
endmodule

module registro_bidireccional (
  input  in_1,
  input  load,
  input  read,
  output s0
);

  wire clock_1_out, controlled_buffer_1_out, not_1_out, registro_salida_restringida_1_s0;

  Clock clock_1 (.out(clock_1_out));
  assign controlled_buffer_1_out = load ? in_1 : 1'bz;  // Controlled_Buffer controlled_buffer_1
  not not_1 (not_1_out, load);
  registro_salida_restringida registro_salida_restringida_1 (
    .i(controlled_buffer_1_out), .load(load), .read(not_1_out), .clk(clock_1_out),
    .s0(registro_salida_restringida_1_s0));
  assign s0 = not_1_out ? registro_salida_restringida_1_s0 : 1'bz;  // Controlled_Buffer controlled_buffer_2
endmodule
