// Logisim project TallerLogica-Combinatorios.circ as structural Verilog: 12 circuits, main circuit verificador
module sumador_simple (
  input  a,
  input  b,
  output S,
  output Cout
);

  xor xor_1 (S, a, b);
  and and_1 (Cout, a, b);
endmodule

module sumador_completo (
  input  Cin,
  input  A,
  input  B,
  output S,
  output Cout
);

  wire sumador_simple_1_cout, sumador_simple_1_s, sumador_simple_2_cout;

  sumador_simple sumador_simple_1 (.a(A), .b(B), .S(sumador_simple_1_s), .Cout(sumador_simple_1_cout));
  sumador_simple sumador_simple_2 (.a(Cin), .b(sumador_simple_1_s), .S(S), .Cout(sumador_simple_2_cout));
  or or_1 (Cout, sumador_simple_2_cout, sumador_simple_1_cout);
endmodule

module sumador_4 (
  input  Cin,
  input  [3:0] A,
  input  [3:0] B,
  output [3:0] S,
  output Cout
);

  wire sumador_completo_1_cout, sumador_completo_2_cout, sumador_completo_3_cout;

  sumador_completo sumador_completo_1 (.A(A[0]), .B(B[0]), .Cin(Cin), .S(S[0]), .Cout(sumador_completo_1_cout));
  sumador_completo sumador_completo_2 (
    .A(A[1]), .B(B[1]), .Cin(sumador_completo_1_cout), .S(S[1]), .Cout(sumador_completo_2_cout));
  sumador_completo sumador_completo_3 (
    .A(A[2]), .B(B[2]), .Cin(sumador_completo_2_cout), .S(S[2]), .Cout(sumador_completo_3_cout));
  sumador_completo sumador_completo_4 (.A(A[3]), .B(B[3]), .Cin(sumador_completo_3_cout), .S(S[3]), .Cout(Cout));
  Hex_Digit_Display hex_digit_display_1 (.value(S));  // open: dp
endmodule

// comp-z
module comparador_cero (
  input  [3:0] A,
  output Z
);

  wire and_1_out, and_2_out, not_1_out, not_2_out, not_3_out, not_4_out;

  not not_1 (not_1_out, A[0]);
  and and_1 (and_1_out, not_1_out, not_2_out);
  not not_2 (not_2_out, A[1]);
  not not_3 (not_3_out, A[2]);
  not not_4 (not_4_out, A[3]);
  and and_2 (and_2_out, not_3_out, not_4_out);
  and and_3 (Z, and_1_out, and_2_out);
endmodule

module sumador_flags (
  input  Cin,
  input  [3:0] A,
  input  [3:0] B,
  output [3:0] S,
  output N,
  output Z,
  output V,
  output C
);

  wire and_1_out, and_2_out, and_3_out, and_4_out, not_1_out, not_2_out, not_3_out;

  sumador_4 sumador_4_1 (.Cin(Cin), .A(A), .S({N, S[2:0]}), .B(B), .Cout(C));
  not not_1 (not_1_out, A[3]);
  not not_2 (not_2_out, B[3]);
  not not_3 (not_3_out, N);
  Hex_Digit_Display hex_digit_display_1 (.value({N, S[2:0]}));  // open: dp
  and and_1 (and_1_out, B[3], A[3]);
  and and_2 (and_2_out, not_1_out, not_2_out);
  comparador_cero comparador_cero_1 (.A({N, S[2:0]}), .Z(Z));
  and and_3 (and_3_out, not_3_out, and_1_out);
  and and_4 (and_4_out, N, and_2_out);
  or or_1 (V, and_3_out, and_4_out);

  assign S[3] = N;
endmodule

module incrementador_4 (
  input  [3:0] A,
  output [3:0] S
);

  sumador_4 sumador_4_1 (.Cin(1'b0), .A(A), .S(S), .B(4'b0001));  // open: Cout
  Hex_Digit_Display hex_digit_display_1 (.value(S));  // open: dp
endmodule

// inv
module inversor_4 (
  input  [3:0] A,
  input  INV,
  output [3:0] S
);

  wire [3:0] incrementador_4_1_s, not_1_out;

  assign not_1_out = ~A;  // NOT_Gate not_1, 4 bits wide
  incrementador_4 incrementador_4_1 (.A(not_1_out), .S(incrementador_4_1_s));
  Multiplexer #(.width(4)) multiplexer_1 (.in0(A), .in1(incrementador_4_1_s), .out(S), .sel(INV));  // open: en
  Hex_Digit_Display hex_digit_display_1 (.value(S));  // open: dp
endmodule

module ALU (
  input  [3:0] A,
  input  [3:0] B,
  input  [1:0] OP,
  output V,
  output C,
  output [3:0] S,
  output N,
  output Z
);

  wire and_1_out, comparador_cero_1_z, not_1_out, not_2_out, sumador_flags_1_c, sumador_flags_1_v, xor_1_out;
  wire [3:0] and_4_1_out_3, inversor_4_1_s, or_4_1_out_3, sumador_flags_1_s;

  inversor_4 inversor_4_1 (.A(B), .INV(and_1_out), .S(inversor_4_1_s));
  and and_1 (and_1_out, not_1_out, OP[0]);
  not not_1 (not_1_out, OP[1]);
  sumador_flags sumador_flags_1 (
    .A(A), .B(inversor_4_1_s), .Cin(1'b0), .S(sumador_flags_1_s), .V(sumador_flags_1_v), .C(sumador_flags_1_c));  // open: N, Z
  Multiplexer #(.select(2)) multiplexer_1 (
    .in0(sumador_flags_1_v), .in1(sumador_flags_1_v), .in2(1'b0), .in3(1'b0), .out(V), .sel(OP));  // open: en
  not not_2 (not_2_out, sumador_flags_1_c);
  Multiplexer #(.select(2)) multiplexer_2 (
    .in0(sumador_flags_1_c), .in1(xor_1_out), .in2(1'b0), .in3(1'b0), .out(C), .sel(OP));  // open: en
  xor xor_1 (xor_1_out, not_2_out, comparador_cero_1_z);
  comparador_cero comparador_cero_1 (.A(B), .Z(comparador_cero_1_z));
  and_4 and_4_1 (.e0(A), .e1(B), .out_3(and_4_1_out_3));
  or_4 or_4_1 (.e0(A), .e1(B), .out_3(or_4_1_out_3));
  Hex_Digit_Display hex_digit_display_1 (.value({N, S[2:0]}));  // open: dp
  Multiplexer #(.select(2), .width(4)) multiplexer_3 (
    .in0(sumador_flags_1_s), .in1(sumador_flags_1_s), .in2(and_4_1_out_3), .in3(or_4_1_out_3),
    .out({N, S[2:0]}), .sel(OP));  // open: en
  comparador_cero comparador_cero_2 (.A({N, S[2:0]}), .Z(Z));

  assign S[3] = N;
endmodule

module verificador (
  output [3:0] a,
  output [3:0] b,
  output [1:0] Op,
  output N,
  output Z,
  output V,
  output C,
  output [3:0] Res,
  output halt
);

  wire clock_1_out;

  Counter #(.width(10), .max('h3ff)) counter_1 (
    .Q({Op, b, a}), .carry(halt), .clk(clock_1_out));  // open: load, D, count, clr
  Clock clock_1 (.out(clock_1_out));
  ALU alu_1 (.A(a), .B(b), .V(V), .C(C), .OP(Op), .S(Res), .N(N), .Z(Z));
endmodule

module decoder (
  input  e1,
  input  e0,
  output s3,
  output s2,
  output s1,
  output s0
);

  wire not_1_out, not_2_out;

  not not_1 (not_1_out, e1);
  not not_2 (not_2_out, e0);
  and and_1 (s3, e1, e0);
  and and_2 (s2, e1, not_2_out);
  and and_3 (s1, not_1_out, e0);
  and and_4 (s0, not_1_out, not_2_out);
endmodule

module and_4 (
  input  [3:0] e0,
  input  [3:0] e1,
  output [3:0] out_3
);

  and and_1 (out_3[0], e0[0], e1[0]);
  and and_2 (out_3[1], e0[1], e1[1]);
  and and_3 (out_3[2], e0[2], e1[2]);
  and and_4 (out_3[3], e0[3], e1[3]);
endmodule

module or_4 (
  input  [3:0] e0,
  input  [3:0] e1,
  output [3:0] out_3
);

  or or_1 (out_3[0], e0[0], e1[0]);
  or or_2 (out_3[1], e0[1], e1[1]);
  or or_3 (out_3[2], e0[2], e1[2]);
  or or_4 (out_3[3], e0[3], e1[3]);
endmodule
